// Logisim project design1.circ as structural Verilog: 1 circuit, main circuit main
module main (
  input  A1,
  input  A0,
  input  B1,
  input  B0,
  output X,
  output Y,
  output Z
);

  wire and_1_out, and_2_out, and_3_out, and_4_out, and_5_out, and_6_out, and_7_out, and_8_out, and_9_out,
       and_10_out, and_11_out, and_12_out, and_13_out, and_14_out, and_15_out, and_16_out, and_17_out,
       and_18_out, and_19_out, not_1_out, not_2_out, not_3_out, not_4_out, not_5_out, not_6_out, not_7_out,
       not_8_out, not_9_out, not_10_out, or_1_out, or_2_out, or_3_out;

  not not_1 (not_1_out, A1);
  not not_2 (not_2_out, A0);
  not not_3 (not_3_out, A0);
  not not_4 (not_4_out, B1);
  not not_5 (not_5_out, B0);
  not not_6 (not_6_out, B1);
  not not_7 (not_7_out, B1);
  not not_8 (not_8_out, A1);
  not not_9 (not_9_out, A0);
  not not_10 (not_10_out, B0);
  and and_1 (and_1_out, not_1_out, not_2_out);
  and and_2 (and_2_out, B1, B0);
  and and_3 (and_3_out, not_4_out, B0);
  and and_4 (and_4_out, A0, B0);
  and and_5 (and_5_out, A1, not_3_out);
  and and_6 (and_6_out, B1, not_5_out);
  and and_7 (and_7_out, A1, not_6_out);
  and and_8 (and_8_out, A0, not_7_out);
  and and_9 (and_9_out, not_8_out, not_9_out);
  and and_10 (and_10_out, B1, B0);
  and and_11 (and_11_out, A1, A0);
  and and_12 (and_12_out, B1, not_10_out);
  and and_13 (and_13_out, A1, and_4_out);
  and and_14 (and_14_out, and_8_out, B0);
  and and_15 (and_15_out, and_9_out, and_10_out);
  and and_16 (and_16_out, and_11_out, and_12_out);
  and and_17 (and_17_out, and_1_out, B1);
  and and_18 (and_18_out, not_1_out, and_2_out);
  and and_19 (and_19_out, and_5_out, and_6_out);
  or or_1 (or_1_out, and_3_out, and_13_out);
  or or_2 (or_2_out, and_7_out, and_14_out);
  or or_3 (or_3_out, and_15_out, and_16_out);
  or or_4 (X, and_17_out, and_18_out);
  or or_5 (Y, or_1_out, and_19_out);
  or or_6 (Z, or_2_out, or_3_out);
endmodule
