// Logisim project design2.circ as structural Verilog: 1 circuit, main circuit main
module main (
  input  O1,
  input  O0,
  input  S,
  input  A1,
  input  A0,
  input  B1,
  input  B0,
  output E,
  output G,
  output L,
  output B,
  output L7,
  output L6,
  output L5,
  output L4,
  output L3,
  output L2,
  output L1,
  output L0,
  output N
);

  wire and_1_out, and_2_out, and_3_out, and_4_out, and_5_out, and_6_out, and_7_out, and_8_out, and_9_out,
       and_10_out, and_11_out, and_12_out, and_13_out, and_14_out, and_15_out, and_16_out, and_17_out,
       and_18_out, and_19_out, and_20_out, and_21_out, and_22_out, n3_to_8_decoder_74138_1_p4,
       n3_to_8_decoder_74138_1_p5, n3_to_8_decoder_74138_1_p6, n3_to_8_decoder_74138_2_p10,
       n3_to_8_decoder_74138_2_p11, n3_to_8_decoder_74138_2_p12, n3_to_8_decoder_74138_2_p13,
       n3_to_8_decoder_74138_2_p14, n3_to_8_decoder_74138_2_p15, n3_to_8_decoder_74138_2_p16,
       n3_to_8_decoder_74138_4_p6, n3_to_8_decoder_74138_4_p7, n3_to_8_decoder_74138_4_p10,
       n3_to_8_decoder_74138_6_p6, n3_to_8_decoder_74138_6_p7, n3_to_8_decoder_74138_8_p6,
       n3_to_8_decoder_74138_8_p7, n3_to_8_decoder_74138_10_p6, n3_to_8_decoder_74138_10_p7,
       n3_to_8_decoder_74138_11_p4, n3_to_8_decoder_74138_11_p5, n3_to_8_decoder_74138_11_p6,
       n3_to_8_decoder_74138_11_p7, n3_to_8_decoder_74138_11_p8, n3_to_8_decoder_74138_11_p9,
       n3_to_8_decoder_74138_11_p10, n3_to_8_decoder_74138_11_p11, n3_to_8_decoder_74138_11_p12,
       n3_to_8_decoder_74138_11_p13, n3_to_8_decoder_74138_11_p14, n3_to_8_decoder_74138_11_p15,
       n3_to_8_decoder_74138_11_p16, n3_to_8_decoder_74138_11_p17, n3_to_8_decoder_74138_11_p18,
       n3_to_8_decoder_74138_12_p6, n3_to_8_decoder_74138_12_p7, not_1_out, not_2_out, not_3_out, not_4_out,
       not_5_out, not_6_out, not_7_out, not_8_out, not_9_out, not_10_out, not_11_out, not_12_out, not_13_out,
       not_14_out, not_20_out, not_21_out, not_22_out, not_23_out, not_24_out, not_25_out, not_30_out,
       not_32_out, not_36_out, not_38_out, not_39_out, not_40_out, not_41_out, not_43_out, not_44_out,
       not_45_out, not_46_out, not_47_out, not_48_out, not_49_out, not_50_out, not_52_out, not_53_out,
       not_54_out, not_55_out, not_56_out, not_57_out, not_58_out, not_59_out, not_60_out, not_61_out,
       not_62_out, not_63_out, not_64_out, not_65_out, not_66_out, not_67_out, not_69_out, not_70_out,
       not_71_out, not_72_out, not_73_out, not_74_out, not_75_out, not_76_out, not_93_out, not_95_out,
       not_96_out, not_97_out, not_98_out, not_99_out, not_100_out, not_101_out, not_102_out, not_103_out,
       not_104_out, not_105_out, not_106_out, not_107_out, not_108_out, not_109_out, not_110_out,
       not_111_out, not_112_out, not_113_out, not_114_out, not_115_out, not_116_out, not_117_out,
       not_118_out, not_119_out, not_120_out, or_1_out, or_2_out, or_3_out, or_4_out, or_5_out, or_6_out,
       or_7_out, or_8_out, or_9_out, or_10_out, or_11_out, or_12_out, or_13_out, or_14_out, or_15_out,
       or_16_out, or_17_out, or_19_out, or_20_out, or_21_out, or_22_out, or_23_out, or_24_out, or_25_out,
       or_26_out, or_27_out, or_28_out, or_29_out, or_30_out, or_31_out, or_32_out, or_33_out, or_34_out,
       or_35_out, or_36_out, or_37_out, or_38_out, or_39_out, or_40_out, or_41_out, or_42_out, or_43_out,
       or_44_out, or_45_out, or_46_out, or_47_out, or_48_out, or_49_out, or_51_out, or_53_out, or_56_out,
       or_57_out, or_58_out, or_59_out, or_60_out, or_61_out, or_62_out, or_63_out, or_64_out, or_65_out,
       or_66_out, or_67_out, or_68_out, or_69_out, or_70_out, or_72_out, or_76_out, or_77_out, or_79_out,
       or_80_out;

  not not_1 (not_1_out, O1);
  not not_2 (not_2_out, O0);
  not not_3 (not_3_out, O1);
  not not_4 (not_4_out, O0);
  not not_5 (not_5_out, O0);
  and and_1 (and_1_out, not_1_out, not_2_out);
  and and_2 (and_2_out, not_3_out, O0);
  and and_3 (and_3_out, not_4_out, O1);
  and and_4 (and_4_out, not_5_out, O1);
  not not_6 (not_6_out, S);
  and and_5 (and_5_out, O0, O1);
  and and_6 (and_6_out, O0, O1);
  not not_7 (not_7_out, S);
  not not_8 (not_8_out, A1);
  and and_7 (and_7_out, and_3_out, S);
  and and_8 (and_8_out, and_4_out, not_6_out);
  and and_9 (and_9_out, and_5_out, S);
  and and_10 (and_10_out, and_6_out, not_7_out);
  not not_9 (not_9_out, A1);
  not not_10 (not_10_out, A1);
  not not_11 (not_11_out, A1);
  not not_12 (not_12_out, A1);
  not not_13 (not_13_out, A1);
  and and_11 (and_11_out, not_8_out, and_1_out);
  and and_12 (and_12_out, and_1_out, A1);
  and and_13 (and_13_out, not_9_out, and_2_out);
  and and_14 (and_14_out, and_2_out, A1);
  and and_15 (and_15_out, and_7_out, A1);
  and and_16 (and_16_out, and_8_out, A1);
  and and_17 (and_17_out, and_9_out, A1);
  and and_18 (and_18_out, and_10_out, A1);
  and and_19 (and_19_out, not_10_out, and_7_out);
  and and_20 (and_20_out, not_11_out, and_8_out);
  and and_21 (and_21_out, not_12_out, and_9_out);
  and and_22 (and_22_out, not_13_out, and_10_out);
  // _3_to_8_decoder__74138 #(.Facing("east")) 3_to_8_decoder_74138_1: pin names not known; wires that end beside it: B0, B1, A0, n3_to_8_decoder_74138_1_p4, n3_to_8_decoder_74138_1_p5, n3_to_8_decoder_74138_1_p6
  not not_14 (not_14_out, 1'b1);
  // _3_to_8_decoder__74138 #(.Facing("east")) 3_to_8_decoder_74138_2: pin names not known; wires that end beside it: B0, B1, A0, and_11_out, and_12_out, not_14_out, not_14_out, not_14_out, not_14_out, n3_to_8_decoder_74138_2_p10, n3_to_8_decoder_74138_2_p11, n3_to_8_decoder_74138_2_p12, n3_to_8_decoder_74138_2_p13, n3_to_8_decoder_74138_2_p14, n3_to_8_decoder_74138_2_p15, n3_to_8_decoder_74138_2_p16
  // _3_to_8_decoder__74138 #(.Facing("east")) 3_to_8_decoder_74138_3: pin names not known; wires that end beside it: B0, B1, A0
  // _3_to_8_decoder__74138 #(.Facing("east")) 3_to_8_decoder_74138_4: pin names not known; wires that end beside it: B0, B1, A0, and_13_out, and_14_out, n3_to_8_decoder_74138_4_p6, n3_to_8_decoder_74138_4_p7, n3_to_8_decoder_74138_4_p6, n3_to_8_decoder_74138_4_p7, n3_to_8_decoder_74138_4_p10
  not not_15 (n3_to_8_decoder_74138_4_p7, 1'b1);
  // _3_to_8_decoder__74138 #(.Facing("east")) 3_to_8_decoder_74138_5: pin names not known; wires that end beside it: B0, B1, A0
  // _3_to_8_decoder__74138 #(.Facing("east")) 3_to_8_decoder_74138_6: pin names not known; wires that end beside it: B0, B1, A0, and_19_out, and_15_out, n3_to_8_decoder_74138_6_p6, n3_to_8_decoder_74138_6_p7, n3_to_8_decoder_74138_6_p6, n3_to_8_decoder_74138_6_p7
  not not_16 (n3_to_8_decoder_74138_6_p7, 1'b1);
  // _3_to_8_decoder__74138 #(.Facing("east")) 3_to_8_decoder_74138_7: pin names not known; wires that end beside it: B0, B1, A0
  // _3_to_8_decoder__74138 #(.Facing("east")) 3_to_8_decoder_74138_8: pin names not known; wires that end beside it: B0, B1, A0, and_20_out, and_16_out, n3_to_8_decoder_74138_8_p6, n3_to_8_decoder_74138_8_p7, n3_to_8_decoder_74138_8_p6, n3_to_8_decoder_74138_8_p7
  not not_17 (n3_to_8_decoder_74138_8_p7, 1'b1);
  // _3_to_8_decoder__74138 #(.Facing("east")) 3_to_8_decoder_74138_9: pin names not known; wires that end beside it: B0, B1, A0
  // _3_to_8_decoder__74138 #(.Facing("east")) 3_to_8_decoder_74138_10: pin names not known; wires that end beside it: B0, B1, A0, and_21_out, and_17_out, n3_to_8_decoder_74138_10_p6, n3_to_8_decoder_74138_10_p7, n3_to_8_decoder_74138_10_p6, n3_to_8_decoder_74138_10_p7
  not not_18 (n3_to_8_decoder_74138_10_p7, 1'b1);
  // _3_to_8_decoder__74138 #(.Facing("east")) 3_to_8_decoder_74138_11: pin names not known; wires that end beside it: B0, B1, A0, n3_to_8_decoder_74138_11_p4, n3_to_8_decoder_74138_11_p5, n3_to_8_decoder_74138_11_p6, n3_to_8_decoder_74138_11_p7, n3_to_8_decoder_74138_11_p8, n3_to_8_decoder_74138_11_p9, n3_to_8_decoder_74138_11_p10, n3_to_8_decoder_74138_11_p11, n3_to_8_decoder_74138_11_p12, n3_to_8_decoder_74138_11_p13, n3_to_8_decoder_74138_11_p14, n3_to_8_decoder_74138_11_p15, n3_to_8_decoder_74138_11_p16, n3_to_8_decoder_74138_11_p17, n3_to_8_decoder_74138_11_p18
  // _3_to_8_decoder__74138 #(.Facing("east")) 3_to_8_decoder_74138_12: pin names not known; wires that end beside it: B0, B1, A0, and_22_out, and_18_out, n3_to_8_decoder_74138_12_p6, n3_to_8_decoder_74138_12_p7, n3_to_8_decoder_74138_12_p6, n3_to_8_decoder_74138_12_p7
  not not_19 (n3_to_8_decoder_74138_12_p7, 1'b1);
  // NOT_Gate not_20 has open pins: in=open, out=not_20_out
  // NOT_Gate not_21 has open pins: in=open, out=not_21_out
  // NOT_Gate not_22 has open pins: in=open, out=not_22_out
  // NOT_Gate not_23 has open pins: in=open, out=not_23_out
  // NOT_Gate not_24 has open pins: in=open, out=not_24_out
  // NOT_Gate not_25 has open pins: in=open, out=not_25_out
  // NOT_Gate not_26 is placed but not wired
  // NOT_Gate not_27 is placed but not wired
  // NOT_Gate not_28 is placed but not wired
  // NOT_Gate not_29 is placed but not wired
  // NOT_Gate not_30 has open pins: in=open, out=not_30_out
  // NOT_Gate not_31 is placed but not wired
  // NOT_Gate not_32 has open pins: in=open, out=not_32_out
  // NOT_Gate not_33 is placed but not wired
  not not_34 (n3_to_8_decoder_74138_4_p6, 1'b1);
  // NOT_Gate not_35 is placed but not wired
  // NOT_Gate not_36 has open pins: in=open, out=not_36_out
  // NOT_Gate not_37 is placed but not wired
  // NOT_Gate not_38 has open pins: in=open, out=not_38_out
  // NOT_Gate not_39 has open pins: in=open, out=not_39_out
  // NOT_Gate not_40 has open pins: in=open, out=not_40_out
  // NOT_Gate not_41 has open pins: in=open, out=not_41_out
  // NOT_Gate not_42 has open pins: in=open, out=n3_to_8_decoder_74138_4_p10
  // NOT_Gate not_43 has open pins: in=open, out=not_43_out
  // NOT_Gate not_44 has open pins: in=open, out=not_44_out
  // NOT_Gate not_45 has open pins: in=open, out=not_45_out
  // NOT_Gate not_46 has open pins: in=open, out=not_46_out
  // NOT_Gate not_47 has open pins: in=open, out=not_47_out
  // NOT_Gate not_48 has open pins: in=open, out=not_48_out
  // NOT_Gate not_49 has open pins: in=open, out=not_49_out
  // NOT_Gate not_50 has open pins: in=open, out=not_50_out
  not not_51 (n3_to_8_decoder_74138_6_p6, 1'b1);
  // NOT_Gate not_52 has open pins: in=open, out=not_52_out
  // NOT_Gate not_53 has open pins: in=open, out=not_53_out
  // NOT_Gate not_54 has open pins: in=open, out=not_54_out
  // NOT_Gate not_55 has open pins: in=open, out=not_55_out
  // NOT_Gate not_56 has open pins: in=open, out=not_56_out
  // NOT_Gate not_57 has open pins: in=open, out=not_57_out
  // NOT_Gate not_58 has open pins: in=open, out=not_58_out
  // NOT_Gate not_59 has open pins: in=open, out=not_59_out
  // NOT_Gate not_60 has open pins: in=open, out=not_60_out
  // NOT_Gate not_61 has open pins: in=open, out=not_61_out
  // NOT_Gate not_62 has open pins: in=open, out=not_62_out
  // NOT_Gate not_63 has open pins: in=open, out=not_63_out
  // NOT_Gate not_64 has open pins: in=open, out=not_64_out
  // NOT_Gate not_65 has open pins: in=open, out=not_65_out
  // NOT_Gate not_66 has open pins: in=open, out=not_66_out
  // NOT_Gate not_67 has open pins: in=open, out=not_67_out
  not not_68 (n3_to_8_decoder_74138_8_p6, 1'b1);
  // NOT_Gate not_69 has open pins: in=open, out=not_69_out
  // NOT_Gate not_70 has open pins: in=open, out=not_70_out
  // NOT_Gate not_71 has open pins: in=open, out=not_71_out
  // NOT_Gate not_72 has open pins: in=open, out=not_72_out
  // NOT_Gate not_73 has open pins: in=open, out=not_73_out
  // NOT_Gate not_74 has open pins: in=open, out=not_74_out
  // NOT_Gate not_75 has open pins: in=open, out=not_75_out
  // NOT_Gate not_76 has open pins: in=open, out=not_76_out
  // NOT_Gate not_77 has open pins: in=open, out=n3_to_8_decoder_74138_11_p4
  // NOT_Gate not_78 has open pins: in=open, out=n3_to_8_decoder_74138_11_p5
  // NOT_Gate not_79 has open pins: in=open, out=n3_to_8_decoder_74138_11_p6
  // NOT_Gate not_80 has open pins: in=open, out=n3_to_8_decoder_74138_11_p7
  // NOT_Gate not_81 has open pins: in=open, out=n3_to_8_decoder_74138_11_p8
  // NOT_Gate not_82 has open pins: in=open, out=n3_to_8_decoder_74138_11_p9
  // NOT_Gate not_83 has open pins: in=open, out=n3_to_8_decoder_74138_11_p10
  // NOT_Gate not_84 has open pins: in=open, out=n3_to_8_decoder_74138_11_p11
  not not_85 (n3_to_8_decoder_74138_10_p6, 1'b1);
  // NOT_Gate not_86 has open pins: in=open, out=n3_to_8_decoder_74138_11_p12
  // NOT_Gate not_87 has open pins: in=open, out=n3_to_8_decoder_74138_11_p13
  // NOT_Gate not_88 has open pins: in=open, out=n3_to_8_decoder_74138_11_p14
  // NOT_Gate not_89 has open pins: in=open, out=n3_to_8_decoder_74138_11_p15
  // NOT_Gate not_90 has open pins: in=open, out=n3_to_8_decoder_74138_11_p16
  // NOT_Gate not_91 has open pins: in=open, out=n3_to_8_decoder_74138_11_p17
  // NOT_Gate not_92 has open pins: in=open, out=n3_to_8_decoder_74138_11_p18
  // NOT_Gate not_93 has open pins: in=open, out=not_93_out
  not not_94 (n3_to_8_decoder_74138_12_p6, 1'b1);
  not not_95 (not_95_out, n3_to_8_decoder_74138_2_p11);
  not not_96 (not_96_out, n3_to_8_decoder_74138_2_p15);
  // NOT_Gate not_97 has open pins: in=open, out=not_97_out
  // NOT_Gate not_98 has open pins: in=open, out=not_98_out
  // NOT_Gate not_99 has open pins: in=open, out=not_99_out
  // NOT_Gate not_100 has open pins: in=open, out=not_100_out
  // NOT_Gate not_101 has open pins: in=open, out=not_101_out
  // NOT_Gate not_102 has open pins: in=open, out=not_102_out
  // NOT_Gate not_103 has open pins: in=open, out=not_103_out
  // NOT_Gate not_104 has open pins: in=open, out=not_104_out
  // NOT_Gate not_105 has open pins: in=open, out=not_105_out
  // NOT_Gate not_106 has open pins: in=open, out=not_106_out
  // NOT_Gate not_107 has open pins: in=open, out=not_107_out
  // NOT_Gate not_108 has open pins: in=open, out=not_108_out
  // NOT_Gate not_109 has open pins: in=open, out=not_109_out
  // NOT_Gate not_110 has open pins: in=open, out=not_110_out
  // NOT_Gate not_111 has open pins: in=open, out=not_111_out
  // NOT_Gate not_112 has open pins: in=open, out=not_112_out
  or or_1 (or_1_out, not_43_out, not_44_out);
  or or_2 (or_2_out, not_47_out, not_48_out);
  or or_3 (or_3_out, not_52_out, not_53_out);
  or or_4 (or_4_out, not_56_out, not_57_out);
  or or_5 (or_5_out, not_60_out, not_61_out);
  or or_6 (or_6_out, not_62_out, not_63_out);
  or or_7 (or_7_out, not_64_out, not_65_out);
  or or_8 (or_8_out, not_66_out, not_67_out);
  or or_9 (or_9_out, not_69_out, not_70_out);
  or or_10 (or_10_out, not_71_out, not_72_out);
  or or_11 (or_11_out, not_73_out, not_74_out);
  or or_12 (or_12_out, not_75_out, not_76_out);
  or or_13 (or_13_out, not_98_out, not_101_out);
  or or_14 (or_14_out, not_99_out, not_102_out);
  or or_15 (or_15_out, not_100_out, not_103_out);
  or or_16 (or_16_out, not_106_out, not_109_out);
  or or_17 (or_17_out, not_104_out, not_107_out);
  or or_18 (L5, not_108_out, not_111_out);
  not not_113 (not_113_out, n3_to_8_decoder_74138_2_p16);
  not not_114 (not_114_out, n3_to_8_decoder_74138_2_p12);
  not not_115 (not_115_out, n3_to_8_decoder_74138_1_p5);
  not not_116 (not_116_out, n3_to_8_decoder_74138_2_p10);
  not not_117 (not_117_out, n3_to_8_decoder_74138_2_p13);
  not not_118 (not_118_out, n3_to_8_decoder_74138_2_p14);
  or or_19 (or_19_out, not_30_out, not_32_out);
  or or_20 (or_20_out, not_36_out, not_38_out);
  or or_21 (or_21_out, not_39_out, not_40_out);
  or or_22 (or_22_out, not_41_out, n3_to_8_decoder_74138_4_p10);
  or or_23 (or_23_out, or_1_out, or_24_out);
  or or_24 (or_24_out, not_45_out, not_46_out);
  or or_25 (or_25_out, or_2_out, or_26_out);
  or or_26 (or_26_out, not_49_out, not_50_out);
  or or_27 (or_27_out, or_3_out, or_28_out);
  or or_28 (or_28_out, not_54_out, not_55_out);
  or or_29 (or_29_out, or_4_out, or_30_out);
  or or_30 (or_30_out, not_58_out, not_59_out);
  or or_31 (or_31_out, or_5_out, or_6_out);
  or or_32 (or_32_out, or_7_out, or_8_out);
  or or_33 (or_33_out, or_9_out, or_10_out);
  or or_34 (or_34_out, or_33_out, or_35_out);
  or or_35 (or_35_out, or_11_out, or_12_out);
  or or_36 (or_36_out, or_14_out, not_105_out);
  or or_37 (or_37_out, or_15_out, or_16_out);
  or or_38 (or_38_out, or_17_out, not_110_out);
  not not_119 (not_119_out, n3_to_8_decoder_74138_1_p4);
  or or_39 (or_39_out, not_119_out, not_120_out);
  not not_120 (not_120_out, n3_to_8_decoder_74138_1_p6);
  or or_40 (or_40_out, not_113_out, not_114_out);
  or or_41 (or_41_out, not_115_out, not_117_out);
  or or_42 (or_42_out, not_116_out, not_118_out);
  or or_43 (or_43_out, not_95_out, not_96_out);
  or or_44 (or_44_out, not_20_out, not_21_out);
  or or_45 (or_45_out, not_22_out, not_23_out);
  or or_46 (or_46_out, not_24_out, not_25_out);
  or or_47 (or_47_out, or_19_out, or_20_out);
  or or_48 (or_48_out, or_21_out, or_22_out);
  or or_49 (or_49_out, or_31_out, or_32_out);
  or or_50 (E, or_39_out, or_40_out);
  or or_51 (or_51_out, or_41_out, or_42_out);
  or or_52 (G, or_51_out, or_43_out);
  or or_53 (or_53_out, or_44_out, or_45_out);
  or or_54 (L, or_53_out, or_46_out);
  or or_55 (B, or_47_out, or_48_out);
  or or_56 (or_56_out, n3_to_8_decoder_74138_11_p5, n3_to_8_decoder_74138_11_p6);
  or or_57 (or_57_out, or_56_out, or_58_out);
  or or_58 (or_58_out, n3_to_8_decoder_74138_11_p7, n3_to_8_decoder_74138_11_p10);
  or or_59 (or_59_out, n3_to_8_decoder_74138_11_p11, n3_to_8_decoder_74138_11_p15);
  or or_60 (or_60_out, n3_to_8_decoder_74138_11_p4, n3_to_8_decoder_74138_11_p9);
  or or_61 (or_61_out, or_60_out, or_62_out);
  or or_62 (or_62_out, n3_to_8_decoder_74138_11_p14, not_93_out);
  or or_63 (or_63_out, n3_to_8_decoder_74138_11_p8, n3_to_8_decoder_74138_11_p5);
  or or_64 (or_64_out, or_63_out, or_65_out);
  or or_65 (or_65_out, n3_to_8_decoder_74138_11_p10, n3_to_8_decoder_74138_11_p13);
  or or_66 (or_66_out, n3_to_8_decoder_74138_11_p15, n3_to_8_decoder_74138_11_p18);
  or or_67 (or_67_out, n3_to_8_decoder_74138_11_p6, n3_to_8_decoder_74138_11_p11);
  or or_68 (or_68_out, or_67_out, or_69_out);
  or or_69 (or_69_out, n3_to_8_decoder_74138_11_p12, n3_to_8_decoder_74138_11_p17);
  or or_70 (or_70_out, n3_to_8_decoder_74138_11_p7, n3_to_8_decoder_74138_11_p16);
  or or_71 (N, or_57_out, or_59_out);
  or or_72 (or_72_out, or_64_out, or_66_out);
  not not_121 (L7, 1'b1);
  or or_73 (L6, or_29_out, not_112_out);
  or or_74 (L4, or_27_out, or_38_out);
  or or_75 (L3, or_70_out, or_37_out);
  or or_76 (or_76_out, or_25_out, or_68_out);
  or or_77 (or_77_out, or_72_out, or_13_out);
  or or_78 (L1, or_34_out, or_77_out);
  or or_79 (or_79_out, or_23_out, or_49_out);
  or or_80 (or_80_out, or_61_out, not_97_out);
  or or_81 (L2, or_76_out, or_36_out);
  or or_82 (L0, or_79_out, or_80_out);
endmodule
